# Fritzing sketch 2020-11-24_testPullupResistors_3AHME (saved by Fritzing 0.9.4)
breadboards: 1

parts:
  S1 = Pushbutton [package="[SMD]"]
  LED1 = LED - 5mm [color="Red (633nm)" package="5 mm [THT]"]
  Bauteil1 = Arduino Mega 2560 (Rev3)
  R1 = Resistor [tolerance=±5% resistance=330 package="0402 [SMD]"]

nets:
  N1: S1.Pin_1, S1.Pin_2
  N2: S1.Pin_3, S1.Pin_4
  N3: LED1.cathode, R1.Pin_1
  N4: LED1.anode, Bauteil1.D13_PWM
  N5: Bauteil1.GND, R1.Pin_0
