# Fritzing sketch 7Segmentanzeige (saved by Fritzing 0.9.3b)
breadboards: 1

parts:
  Bauteil1 = Arduino Mega 2560 (Rev3)
  R1 = Resistor [tolerance=±5% resistance=220 package=THT]
  R2 = Resistor [tolerance=±5% resistance=220 package=THT]
  R3 = Resistor [tolerance=±5% resistance=220 package=THT]
  R4 = Resistor [tolerance=±5% resistance=220 package=THT]
  R5 = Resistor [tolerance=±5% resistance=220 package=THT]
  R6 = Resistor [tolerance=±5% resistance=220 package=THT]
  R7 = Resistor [tolerance=±5% resistance=220 package=THT]
  R8 = Resistor [tolerance=±5% resistance=220 package=THT]
  DI1 = 7-Segment LED Display [package=THT]

nets:
  N1: Bauteil1.D22, R1.Pin_1
  N2: Bauteil1.D23, R2.Pin_1
  N3: Bauteil1.D24, R3.Pin_1
  N4: Bauteil1.D25, R4.Pin_1
  N5: Bauteil1.D26, R5.Pin_1
  N6: Bauteil1.D27, R6.Pin_1
  N7: Bauteil1.D28, R7.Pin_1
  N8: Bauteil1.D29, R8.Pin_1
  N9: Bauteil1.GND, DI1.commAnode
  N10: R1.Pin_0, DI1.cathodeA
  N11: R2.Pin_0, DI1.cathodeB
  N12: R3.Pin_0, DI1.cathodeC
  N13: R4.Pin_0, DI1.cathodeD
  N14: R5.Pin_0, DI1.cathodeE
  N15: R6.Pin_0, DI1.cathodeF
  N16: R7.Pin_0, DI1.cathodeG
  N17: R8.Pin_0, DI1.cathodeDP
